// Logisim project 20240209-4bitaddsub.circ as structural Verilog
module sum_bit (
  input  A,
  input  B,
  input  Cin,
  output Sum
);

  wire and_1_out, and_2_out, and_3_out, and_4_out;

  and and_1 (and_1_out, ~A, ~B, Cin);  // AND_Gate
  and and_2 (and_2_out, ~A, B, ~Cin);  // AND_Gate
  and and_3 (and_3_out, A, ~B, ~Cin);  // AND_Gate
  and and_4 (and_4_out, A, B, Cin);
  or or_1 (Sum, and_1_out, and_2_out, and_3_out, and_4_out);

  // Notes on the sheet:
  //   Sum-Bit Circuit
endmodule

module cout_bit (
  input  A,
  input  B,
  input  Cin,
  output Cout
);

  wire and_1_out, and_2_out, and_3_out, and_4_out;

  and and_1 (and_1_out, ~A, B, Cin);  // AND_Gate
  and and_2 (and_2_out, A, ~B, Cin);  // AND_Gate
  and and_3 (and_3_out, A, B, ~Cin);  // AND_Gate
  and and_4 (and_4_out, A, B, Cin);
  or or_1 (Cout, and_1_out, and_2_out, and_3_out, and_4_out);

  // Notes on the sheet:
  //   Cout-Bit Circuit
endmodule

module full_adder (
  input  A,
  input  B,
  input  Cin,
  output Cout,
  output Sum
);

  cout_bit cout_bit_1 (.Cout(Cout), .A(A), .B(B), .Cin(Cin));
  sum_bit sum_bit_1 (.Sum(Sum), .A(A), .B(B), .Cin(Cin));

  // Notes on the sheet:
  //   Full Adder Circuit
endmodule

module _4bit_adder (
  input  A3,
  input  A2,
  input  A1,
  input  A0,
  input  B3,
  input  B2,
  input  B1,
  input  B0,
  output Cout,
  output Sum3,
  output Sum2,
  output Sum1,
  output Sum0
);

  wire full_adder_2_cout, full_adder_3_cout, full_adder_4_cout;

  full_adder full_adder_1 (.A(A3), .B(B3), .Cin(full_adder_2_cout), .Cout(Cout), .Sum(Sum3));
  full_adder full_adder_2 (.A(A2), .B(B2), .Cin(full_adder_3_cout), .Cout(full_adder_2_cout), .Sum(Sum2));
  full_adder full_adder_3 (.A(A1), .B(B1), .Cin(full_adder_4_cout), .Cout(full_adder_3_cout), .Sum(Sum1));
  full_adder full_adder_4 (.A(A0), .B(B0), .Cin(1'b0), .Cout(full_adder_4_cout), .Sum(Sum0));

  // Notes on the sheet:
  //   4-bit Adder Circuit
  //   Ground
endmodule

module XOR (
  input  A,
  input  B,
  output out_3
);

  xor xor_1 (out_3, A, B);

  // Notes on the sheet:
  //   A + B = (+A) + (+B)
  //   A - B = (+A) + (-B)
endmodule

module _4bit_add_sub (
  input  A3,
  input  A2,
  input  A1,
  input  A0,
  input  _2_s_Comp__Switch,
  input  B3,
  input  B2,
  input  B1,
  input  B0,
  output Cout,
  output Sum3,
  output Sum2,
  output Sum1,
  output Sum0
);

  wire full_adder_2_cout, full_adder_3_cout, full_adder_4_cout, xor_1_out, xor_2_out, xor_3_out, xor_4_out;

  xor xor_1 (xor_1_out, A3, _2_s_Comp__Switch);
  full_adder full_adder_1 (.A(xor_1_out), .B(B3), .Cin(full_adder_2_cout), .Cout(Cout), .Sum(Sum3));
  xor xor_2 (xor_2_out, A2, _2_s_Comp__Switch);
  full_adder full_adder_2 (.A(xor_2_out), .B(B2), .Cin(full_adder_3_cout), .Cout(full_adder_2_cout), .Sum(Sum2));
  xor xor_3 (xor_3_out, A1, _2_s_Comp__Switch);
  full_adder full_adder_3 (.A(xor_3_out), .B(B1), .Cin(full_adder_4_cout), .Cout(full_adder_3_cout), .Sum(Sum1));
  xor xor_4 (xor_4_out, A0, _2_s_Comp__Switch);
  full_adder full_adder_4 (.A(xor_4_out), .B(B0), .Cin(_2_s_Comp__Switch), .Cout(full_adder_4_cout), .Sum(Sum0));

  // Notes on the sheet:
  //   4-bit Adder Subtractor
  //   two's complement:
  //   1. Invert bits
  //   2. Add 1
  //   "A" is signed binary number
  //   - If "A" is negative,
  //   enter the positive value in circuit
  //   then turn "Switch" to 1.
  //   "B" is signed binary number,
  //   - If "A" is positive, "Switch" should be 0.
  //   but in this circuit is always positive.
endmodule
