// Logisim project circuit.circ as structural Verilog: 8 circuits, main circuit main
module main (
  input  A,
  input  B,
  output out_3,
  output out_4
);

  and and_1 (out_3, A, B);
  or or_1 (out_4, A, B);
endmodule

module sumbit (
  input  A,
  input  B,
  input  Cin,
  output out_4
);

  wire and_1_out, and_2_out, and_3_out, and_4_out;

  and and_1 (and_1_out, ~A, ~B, Cin);  // AND_Gate
  and and_2 (and_2_out, ~A, B, ~Cin);  // AND_Gate
  and and_3 (and_3_out, A, ~B, ~Cin);  // AND_Gate
  and and_4 (and_4_out, A, B, Cin);
  or or_1 (out_4, and_1_out, and_2_out, and_3_out, and_4_out);

  // Notes on the sheet:
  //   Sumbit circuit
endmodule

module cout (
  input  A,
  input  B,
  input  Cin,
  output out_4
);

  wire and_1_out, and_2_out, and_3_out, and_4_out;

  and and_1 (and_1_out, ~A, B, Cin);  // AND_Gate
  and and_2 (and_2_out, A, ~B, Cin);  // AND_Gate
  and and_3 (and_3_out, A, B, ~Cin);  // AND_Gate
  and and_4 (and_4_out, A, B, Cin);
  or or_1 (out_4, and_1_out, and_2_out, and_3_out, and_4_out);

  // Notes on the sheet:
  //   C out
endmodule

module fulladder (
  input  A,
  input  B,
  input  Cin,
  output Cout,
  output Sum
);

  cout c_out (.out_4(Cout), .A(A), .B(B), .Cin(Cin));
  sumbit sumbit (.out_4(Sum), .A(A), .B(B), .Cin(Cin));

  // Notes on the sheet:
  //   Full adder circuit
endmodule

module _4bit_adder (
  input  A3,
  input  B3,
  input  A2,
  input  B2,
  input  A1,
  input  B1,
  input  A0,
  input  B0,
  output c_out,
  output sum_3,
  output sum_2,
  output sum_1,
  output sum_0
);

  wire fulladder_2_cout, fulladder_3_cout, fulladder_4_cout;

  fulladder fulladder_1 (.A(A3), .B(B3), .Cin(fulladder_2_cout), .Cout(c_out), .Sum(sum_3));
  fulladder fulladder_2 (.A(A2), .B(B2), .Cin(fulladder_3_cout), .Cout(fulladder_2_cout), .Sum(sum_2));
  fulladder fulladder_3 (.A(A1), .B(B1), .Cin(fulladder_4_cout), .Cout(fulladder_3_cout), .Sum(sum_1));
  fulladder fulladder_4 (.A(A0), .B(B0), .Cin(1'b0), .Cout(fulladder_4_cout), .Sum(sum_0));
endmodule

module subtractbit (
  input  in_1,
  input  in_2,
  output out_3
);

  xor xor_1 (out_3, in_1, in_2);
endmodule

module _4bit_adder_subtractor (
  input  A3,
  input  A2,
  input  A1,
  input  A0,
  input  switch,
  input  B3,
  input  B2,
  input  B1,
  input  B0,
  output A3_flipped,
  output A2_flipped,
  output A1_flipped,
  output A0_flipped,
  output c_out,
  output sum_3,
  output sum_2,
  output sum_1,
  output sum_0
);

  wire fulladder_2_cout, fulladder_3_cout, fulladder_4_cout;

  fulladder fulladder_1 (.A(A3_flipped), .B(B3), .Cin(fulladder_2_cout), .Cout(c_out), .Sum(sum_3));
  xor xor_1 (A3_flipped, A3, switch);
  fulladder fulladder_2 (.A(A2_flipped), .B(B2), .Cin(fulladder_3_cout), .Cout(fulladder_2_cout), .Sum(sum_2));
  xor xor_2 (A1_flipped, A1, switch);
  xor xor_3 (A2_flipped, A2, switch);
  fulladder fulladder_3 (.A(A1_flipped), .B(B1), .Cin(fulladder_4_cout), .Cout(fulladder_3_cout), .Sum(sum_1));
  xor xor_4 (A0_flipped, A0, switch);
  fulladder fulladder_4 (.A(A0_flipped), .B(B0), .Cin(switch), .Cout(fulladder_4_cout), .Sum(sum_0));

  // Notes on the sheet:
  //   4-bit Adder/Subtractor Circuit
  //   B is an unsigned number 
  //   Turn on flipped the A signed number
  //   A is a signed number (can be positve and negative)
endmodule

module car_alarm (
  input  K,
  input  D,
  input  B,
  output out_4
);

  wire and_1_out, and_2_out, and_3_out;

  and and_1 (and_1_out, K, ~D, ~B);  // AND_Gate
  and and_2 (and_2_out, K, ~D, B);  // AND_Gate
  and and_3 (and_3_out, K, D, ~B);  // AND_Gate
  or or_1 (out_4, and_1_out, and_2_out, and_3_out);
endmodule
