// Logisim project microproc.circ as structural Verilog: 1 circuit, main circuit main
module main (
  input  CLK,
  input  [7:0] Data,
  input  S1,
  input  S0,
  input  in_5,
  input  in_6,
  output [7:0] out_7
);

  wire and_1_out, and_2_out, and_3_out, and_4_out, decoder_1_out0, decoder_1_out1, decoder_1_out2,
       decoder_1_out3;
  wire [7:0] R0_q, R1_q, R2_q, R3_q;

  Decoder #(.select(2)) decoder_1 (
    .out0(decoder_1_out0), .out1(decoder_1_out1), .out2(decoder_1_out2), .out3(decoder_1_out3), .sel({S1, S0}));  // open: en
  and and_1 (and_1_out, decoder_1_out0, CLK);
  and and_2 (and_2_out, decoder_1_out1, CLK);
  and and_3 (and_3_out, decoder_1_out2, CLK);
  and and_4 (and_4_out, decoder_1_out3, CLK);
  Register R0 (.D(Data), .Q(R0_q), .clk(and_1_out));  // open: en, clr
  Register R1 (.D(Data), .Q(R1_q), .clk(and_2_out));  // open: en, clr
  Register R2 (.D(Data), .Q(R2_q), .clk(and_3_out));  // open: en, clr
  Register R3 (.D(Data), .Q(R3_q), .clk(and_4_out));  // open: en, clr
  Multiplexer #(.select(2), .width(8)) multiplexer_1 (
    .in0(R0_q), .in1(R1_q), .in2(R2_q), .in3(R3_q), .out(out_7), .sel({in_5, in_6}));  // open: en

  // Notes on the sheet:
  //   R0==>00
  //   R1==> 01
  //   R2==>10
  //   R3==>11
  //   Select which register to write
  //   Select which register to read 
endmodule
