// Logisim project trafficlight.circ as structural Verilog
module main (
  input  in_1,
  input  in_2
);

  // AND_Gate and_1 is placed but not wired
  // AND_Gate and_2 is placed but not wired
  Register #(.width(1)) register_1 ();  // open: D, en, Q, clk, clr
endmodule
