// Logisim project question6_lab6.circ as structural Verilog: 1 circuit, main circuit main
module main (
  input  in_1,
  input  X,
  output Next_state,
  output out_4,
  output out_5,
  output out_6
);

  wire and_1_out, and_2_out, and_3_out, and_4_out;

  and and_1 (and_1_out, ~X, ~out_6, ~out_5);  // AND_Gate
  and and_2 (and_2_out, X, ~out_6, out_5);  // AND_Gate
  and and_3 (and_3_out, ~X, out_6, out_5);  // AND_Gate
  and and_4 (and_4_out, X, out_6, ~out_5);  // AND_Gate
  or or_1 (Next_state, and_1_out, and_2_out, and_3_out, and_4_out);
  not not_1 (out_4, out_5);
  Register #(.width(1)) S0 (.D(out_4), .Q(out_5), .clk(in_1));  // open: en, clr
  Register #(.width(1)) S1 (.D(Next_state), .Q(out_6), .clk(in_1));  // open: en, clr

  // Notes on the sheet:
  //   Harry Do
  //   Current state
endmodule
