// Logisim project seq_circ.circ as structural Verilog: 2 circuits, main circuit main
module main (
  input  CLK,
  input  X,
  output S1,
  output S0,
  output _00,
  output _01,
  output _10,
  output _11,
  output S1_2,
  output S0_2
);

  wire and_1_out, and_2_out, and_3_out, and_4_out;

  and and_1 (and_1_out, ~X, S0_2, ~S1_2);  // AND_Gate
  and and_2 (and_2_out, ~X, ~S0_2, S1_2);  // AND_Gate
  and and_3 (and_3_out, X, ~S0_2, ~S1_2);  // AND_Gate
  and and_4 (and_4_out, X, S0_2, S1_2);
  not not_1 (S0, S0_2);
  or or_1 (S1, and_1_out, and_2_out, and_3_out, and_4_out);
  Register #(.width(1)) u_S0 (.D(S0), .Q(S0_2), .clk(CLK));  // open: en, clr
  Register #(.width(1)) u_S1 (.D(S1), .Q(S1_2), .clk(CLK));  // open: en, clr
  Decoder #(.select(2)) decoder_1 (.out0(_00), .out1(_01), .out2(_10), .out3(_11), .sel({S1_2, S0_2}));  // open: en

  // Notes on the sheet:
  //   Current state
  //   Next state
  //   current state
  //   S0
  //   S1
  //   S2
  //   S3
endmodule

module example2 (
  input  CLK,
  output S2,
  output S1,
  output S0,
  output S2_2,
  output S1_2,
  output S0_2
);

  wire and_1_out, and_2_out, and_3_out, and_4_out;

  and and_1 (and_1_out, S1_2, ~S0_2);  // AND_Gate
  and and_2 (and_2_out, ~S2_2, ~S1_2, S0_2);  // AND_Gate
  and and_3 (and_3_out, S1_2, S0_2);
  and and_4 (and_4_out, S2_2, ~S0_2);  // AND_Gate
  or or_1 (S1, and_1_out, and_2_out);
  or or_2 (S2, and_3_out, and_4_out);
  not not_1 (S0, S0_2);
  Register #(.width(1)) u_S0 (.D(S0), .Q(S0_2), .clk(CLK));  // open: en, clr
  Register #(.width(1)) u_S1 (.D(S1), .Q(S1_2), .clk(CLK));  // open: en, clr
  Register #(.width(1)) u_S2 (.D(S2), .Q(S2_2), .clk(CLK));  // open: en, clr

  // Notes on the sheet:
  //   Next state
  //   Current state
endmodule
