// Logisim project sequential_circuit.circ as structural Verilog: 5 circuits, main circuit SR latch
module SR_latch (
  input  R,
  input  S,
  output Q,
  output nQ
);

  nor nor_1 (Q, R, nQ);
  nor nor_2 (nQ, Q, S);

  // Notes on the sheet:
  //   SR latch
endmodule

module D_latch (
  input  CLK,
  input  D,
  output Q,
  output nQ
);

  wire and_1_out, and_2_out;

  and and_1 (and_1_out, CLK, CLK, ~D);  // AND_Gate
  and and_2 (and_2_out, CLK, D);
  SR_latch sr_latch_1 (.R(and_1_out), .S(and_2_out), .Q(Q), .nQ(nQ));

  // Notes on the sheet:
  //   D-LATCH
endmodule

module _4_bit_d_latch (
  input  in_1,
  input  D3,
  input  D2,
  input  D1,
  input  D0,
  output out_6,
  output out_7,
  output out_8,
  output out_9,
  output out_10,
  output out_11,
  output out_12,
  output out_13
);

  D_latch d_latch_1 (.CLK(in_1), .D(D0), .Q(out_9));  // open: nQ
  // D_latch d_latch_2: pin names not known; wires that end beside it: D1, in_1, out_8, out_11
  // D_latch d_latch_3: pin names not known; wires that end beside it: D2, in_1, out_7, out_12
  // D_latch d_latch_4: pin names not known; wires that end beside it: D3, in_1, out_6, out_13
endmodule

module D___Flip_flop (
  input  CLK,
  input  D,
  output out_3,
  output out_4
);

  wire d_latch_1_q, not_1_out;

  not not_1 (not_1_out, CLK);
  D_latch d_latch_1 (.CLK(not_1_out), .D(D), .Q(d_latch_1_q));  // open: nQ
  D_latch d_latch_2 (.CLK(CLK), .D(d_latch_1_q), .Q(out_3), .nQ(out_4));

  // Notes on the sheet:
  //   N1
  //   DL1
  //   Next Stage
  //   DL2
  //   Current stage
endmodule

module register (
  input  in_1,
  input  in_2
);

  wire d_flip_flop_1_out_3, not_1_out, register_1_q;

  not not_1 (not_1_out, register_1_q);
  Register #(.width(1)) register_1 (.D(not_1_out), .Q(register_1_q), .clk(in_2));  // open: en, clr
  D___Flip_flop d_flip_flop_1 (.D(d_flip_flop_1_out_3), .CLK(in_1), .out_3(d_flip_flop_1_out_3));  // open: out_4
endmodule
