// Logisim project sum of product.circ as structural Verilog: 1 circuit, main circuit main
module main (
  input  A,
  input  B,
  output out_3
);

  wire and_1_out, and_2_out;

  and and_1 (and_1_out, A, ~B);  // AND_Gate
  and and_2 (and_2_out, A, B);
  or or_1 (out_3, and_1_out, and_2_out);

  // Notes on the sheet:
  //   Harry Do
endmodule
